// Digital circuit lab04.dig as structural Verilog
module lab04 (
  input  clk,
  input  rst,
  output [31:0] PC,
  output [5:0] opcode,
  output [4:0] src1__addr,
  output [31:0] src1__out,
  output [4:0] src2__addr,
  output [31:0] src2__out,
  output [4:0] dst__addr,
  output [31:0] dst__data
);

  wire ALU0, aluSrc, and_1_out, Branch, memRead, memReg, memWrite, regDst, writeReg;
  wire [1:0] aluOP;
  wire [3:0] aluCtr;
  wire [5:0] cpumemory_d2;
  wire [15:6] cpumemory_d2_2;
  wire [31:0] aluResult, dataVal, imm, multiplexer_3_out, PC_plus_4, PCNXT, u_alu_2_result;

  gen_register #(.applicationType("IVERILOG"), .CodeFile("./gen_register.v")) u_gen_register (
    .clk(clk), .rst(rst), .write_en(clk), .data_in(PCNXT), .data_out(PC));
  alu #(.applicationType("IVERILOG"), .CodeFile("./alu.v")) u_alu (
    .alu_control(4'b0010), .A(PC), .B(32'h4), .result(PC_plus_4));  // open: zero
  RAMDualAccess #(.AddrBits(8), .isProgramMemory("true"), .Bits(32)) cpumemory (
    .str(memWrite), .C(clk), .ld(memRead), .A1(aluResult[7:0]), .Din1(src2__out), .A2(PC[9:2]), .D1(dataVal),
    .D2({opcode, src1__addr, src2__addr, cpumemory_d2_2, cpumemory_d2}));
  alu #(.applicationType("IVERILOG"), .CodeFile("./alu.v")) u_alu_2 (
    .alu_control(4'b0010), .A({imm[31:2], 2'b00}), .B(PC_plus_4), .result(u_alu_2_result));  // open: zero
  and and_1 (and_1_out, Branch, ALU0);
  Multiplexer #(.Bits(32)) multiplexer_1 (.sel(and_1_out), .in_0(PC_plus_4), .in_1(u_alu_2_result), .out(PCNXT));
  BitExtender #(.inputBits(16), .outputBits(32)) bitextender_1 (.in({cpumemory_d2_2, cpumemory_d2}), .out(imm));
  Multiplexer #(.Bits(5)) multiplexer_2 (
    .sel(regDst), .in_0(src2__addr), .in_1(cpumemory_d2_2[15:11]), .out(dst__addr));
  control_unit #(.applicationType("IVERILOG"), .CodeFile("./control_unit.v")) u_control_unit (
    .instr_op(opcode), .reg_dst(regDst), .branch(Branch), .mem_read(memRead), .mem_to_reg(memReg),
    .alu_op(aluOP), .mem_write(memWrite), .alu_src(aluSrc), .reg_write(writeReg));
  cpu_registers #(.applicationType("IVERILOG"), .CodeFile("./cpu_registers.v")) u_cpu_registers (
    .clk(clk), .rst(rst), .write_en(writeReg), .src1_addr(src1__addr), .src2_addr(src2__addr),
    .dst_addr(dst__addr), .data_in(dst__data), .src1_out(src1__out), .src2_out(src2__out));
  alu_control #(.applicationType("IVERILOG"), .CodeFile("./alu_control.v")) u_alu_control (
    .alu_op(aluOP), .funct(cpumemory_d2), .alu_control(aluCtr));
  Multiplexer #(.Bits(32)) multiplexer_3 (.sel(aluSrc), .in_0(src2__out), .in_1(imm), .out(multiplexer_3_out));
  alu #(.applicationType("IVERILOG"), .CodeFile("./alu.v")) u_alu_3 (
    .alu_control(aluCtr), .A(src1__out), .B(multiplexer_3_out), .zero(ALU0), .result(aluResult));
  Multiplexer #(.Bits(32)) multiplexer_4 (.sel(memReg), .in_0(aluResult), .in_1(dataVal), .out(dst__data));

  // Other names for the same wires on the sheet: Src2Adr[4:0] = src2__addr; Src1Adr[4:0] = src1__addr;
  //   dstData[31:0] = dst__data; Src1Out[31:0] = src1__out; Src2Out[31:0] = src2__out

  // Notes on the sheet:
  //   Inputs
  //   PC
  //   Outputs for testing
endmodule
